// Logisim project DetectorImparDe1s.circ as structural Verilog: 1 circuit, main circuit main
module main (
  input  [3:0] ENTRADA,
  output S
);

  wire and_1_out, and_2_out, and_3_out, and_4_out, and_5_out, and_6_out, and_7_out, and_8_out, not_1_out,
       not_2_out, not_3_out, not_4_out, not_5_out, not_6_out, not_7_out, not_8_out, not_9_out, not_10_out,
       not_11_out, not_12_out, not_13_out, not_14_out, not_15_out, not_16_out;

  not not_1 (not_1_out, ENTRADA[0]);
  not not_2 (not_2_out, ENTRADA[1]);
  not not_3 (not_3_out, ENTRADA[2]);
  not not_4 (not_4_out, ENTRADA[0]);
  not not_5 (not_5_out, ENTRADA[1]);
  not not_6 (not_6_out, ENTRADA[3]);
  not not_7 (not_7_out, ENTRADA[0]);
  not not_8 (not_8_out, ENTRADA[2]);
  not not_9 (not_9_out, ENTRADA[3]);
  not not_10 (not_10_out, ENTRADA[0]);
  not not_11 (not_11_out, ENTRADA[1]);
  not not_12 (not_12_out, ENTRADA[2]);
  not not_13 (not_13_out, ENTRADA[3]);
  not not_14 (not_14_out, ENTRADA[1]);
  not not_15 (not_15_out, ENTRADA[2]);
  not not_16 (not_16_out, ENTRADA[3]);
  and and_1 (and_1_out, not_1_out, not_2_out, not_3_out, ENTRADA[3]);
  and and_2 (and_2_out, not_4_out, not_5_out, ENTRADA[2], not_6_out);
  and and_3 (and_3_out, not_7_out, ENTRADA[1], not_8_out, not_9_out);
  and and_4 (and_4_out, not_10_out, ENTRADA[1], ENTRADA[2], ENTRADA[3]);
  and and_5 (and_5_out, ENTRADA[0], not_11_out, not_12_out, not_13_out);
  and and_6 (and_6_out, ENTRADA[0], not_14_out, ENTRADA[2], ENTRADA[3]);
  and and_7 (and_7_out, ENTRADA[0], ENTRADA[1], not_15_out, ENTRADA[3]);
  and and_8 (and_8_out, ENTRADA[0], ENTRADA[1], ENTRADA[2], not_16_out);
  or or_1 (S, and_1_out, and_2_out, and_3_out, and_4_out, and_5_out, and_6_out, and_7_out, and_8_out);

  // Notes on the sheet:
  //   Tendo numero impar de bits 1, sempre vai ter saida 1
endmodule
