// Logisim project FLIPFLOP.circ as structural Verilog: 3 circuits, main circuit D
module D (
  input  D,
  input  CLK,
  output Q,
  output Q_prime
);

  wire nand_1_out, nand_2_out, nand_3_out, nand_4_out, not_1_out, not_2_out, not_3_out, sr_1_q_prime;

  not not_1 (not_1_out, D);
  nand nand_1 (nand_1_out, D, CLK);
  nand nand_2 (nand_2_out, CLK, not_1_out);
  SR sr_1 (.S(nand_1_out), .R(nand_2_out), .Q_prime(sr_1_q_prime));  // open: Q
  not not_2 (not_2_out, sr_1_q_prime);
  not not_3 (not_3_out, CLK);
  nand nand_3 (nand_3_out, sr_1_q_prime, not_3_out);
  nand nand_4 (nand_4_out, not_3_out, not_2_out);
  SR sr_2 (.S(nand_3_out), .R(nand_4_out), .Q_prime(Q), .Q(Q_prime));
endmodule

module SR (
  input  S,
  input  R,
  output Q_prime,
  output Q
);

  nand nand_1 (Q_prime, S, Q);
  nand nand_2 (Q, Q_prime, R);
endmodule

module JK (
  input  J,
  input  K,
  input  CLK,
  output Q,
  output Q_prime
);

  wire and_1_out, and_2_out, not_1_out, or_1_out;

  not not_1 (not_1_out, K);
  and and_1 (and_1_out, Q_prime, J);
  and and_2 (and_2_out, not_1_out, Q);
  or or_1 (or_1_out, and_1_out, and_2_out);
  D d_1 (.D(or_1_out), .Q(Q), .Q_prime(Q_prime), .CLK(CLK));
endmodule
