// Logisim project MaquinaDeEstados.circ as structural Verilog: 3 circuits, main circuit main
module main (
  input  LIGAR,
  input  \DIF_FAZ_A_MUDANÇA_DE_DIREÇÃO 
);

  wire and_1_out, and_2_out, and_3_out, and_4_out, and_5_out, and_6_out, and_7_out, and_8_out, CLK_out,
       flipfloprs_1_q, flipfloprs_1_q_prime, flipfloprs_2_q, flipfloprs_2_q_prime, not_1_out, or_1_out;

  not not_1 (not_1_out, \DIF_FAZ_A_MUDANÇA_DE_DIREÇÃO );
  and and_1 (and_1_out, flipfloprs_1_q_prime, flipfloprs_2_q_prime, \DIF_FAZ_A_MUDANÇA_DE_DIREÇÃO );
  and and_2 (and_2_out, flipfloprs_1_q_prime, flipfloprs_2_q, not_1_out);
  and and_3 (and_3_out, flipfloprs_1_q, flipfloprs_2_q, \DIF_FAZ_A_MUDANÇA_DE_DIREÇÃO );
  and and_4 (and_4_out, flipfloprs_1_q, flipfloprs_2_q_prime, not_1_out);
  Clock CLK (.out(CLK_out));
  or or_1 (or_1_out, and_1_out, and_2_out, and_3_out, and_4_out);
  and and_5 (and_5_out, flipfloprs_2_q_prime, flipfloprs_1_q_prime);
  LED A (.in(and_5_out));
  and and_6 (and_6_out, flipfloprs_1_q_prime, flipfloprs_2_q);
  LED B (.in(and_6_out));
  flipflopRS flipfloprs_1 (
    .D(or_1_out), .CLK(CLK_out), .Q(flipfloprs_1_q), .Q_prime(flipfloprs_1_q_prime), .ligar(LIGAR));
  and and_7 (and_7_out, flipfloprs_1_q, flipfloprs_2_q_prime);
  LED C (.in(and_7_out));
  and and_8 (and_8_out, flipfloprs_1_q, flipfloprs_2_q);
  LED D (.in(and_8_out));
  flipflopRS flipfloprs_2 (
    .D(flipfloprs_2_q_prime), .CLK(CLK_out), .Q(flipfloprs_2_q), .Q_prime(flipfloprs_2_q_prime), .ligar(LIGAR));
endmodule

module flipflopD (
  input  in_1,
  input  in_2,
  output out_3,
  output out_4
);

  nand nand_1 (out_3, in_1, out_4);
  nand nand_2 (out_4, out_3, in_2);
endmodule

module flipflopRS (
  input  D,
  input  ligar,
  input  CLK,
  output Q,
  output Q_prime
);

  wire and_1_out, flipflopd_1_out_3, nand_1_out, nand_2_out, nand_3_out, nand_4_out, not_1_out, not_2_out,
       not_3_out;

  and and_1 (and_1_out, D, ligar);
  not not_1 (not_1_out, and_1_out);
  nand nand_1 (nand_1_out, and_1_out, CLK);
  nand nand_2 (nand_2_out, CLK, not_1_out);
  flipflopD flipflopd_1 (.in_1(nand_1_out), .in_2(nand_2_out), .out_3(flipflopd_1_out_3));  // open: out_4
  not not_2 (not_2_out, flipflopd_1_out_3);
  not not_3 (not_3_out, CLK);
  nand nand_3 (nand_3_out, flipflopd_1_out_3, not_3_out);
  nand nand_4 (nand_4_out, not_3_out, not_2_out);
  flipflopD flipflopd_2 (.in_1(nand_3_out), .in_2(nand_4_out), .out_3(Q), .out_4(Q_prime));
endmodule
