// Logisim project MemoriaROM.circ as structural Verilog: 1 circuit, main circuit main
module main (
  input  in_1,
  input  in_2,
  input  in_3,
  output [7:0] out_4
);

  wire and_1_out, and_2_out, and_3_out, and_4_out, and_5_out, and_6_out, and_7_out, and_8_out, not_1_out,
       not_2_out, not_3_out, not_4_out, not_5_out, not_6_out, not_7_out, not_8_out, not_9_out, not_10_out,
       not_11_out, not_12_out;

  not not_1 (not_1_out, in_1);
  not not_2 (not_2_out, in_2);
  not not_3 (not_3_out, in_3);
  not not_4 (not_4_out, in_1);
  not not_5 (not_5_out, in_2);
  not not_6 (not_6_out, in_1);
  not not_7 (not_7_out, in_2);
  not not_8 (not_8_out, in_1);
  not not_9 (not_9_out, in_2);
  not not_10 (not_10_out, in_3);
  not not_11 (not_11_out, in_2);
  not not_12 (not_12_out, in_3);
  and and_1 (and_1_out, not_1_out, not_2_out, not_3_out);
  and and_2 (and_2_out, not_4_out, not_5_out, in_3);
  and and_3 (and_3_out, not_6_out, not_7_out, in_3);
  and and_4 (and_4_out, not_8_out, in_2, in_3);
  and and_5 (and_5_out, in_1, not_9_out, not_10_out);
  and and_6 (and_6_out, in_1, not_11_out, in_3);
  and and_7 (and_7_out, in_1, in_2, not_12_out);
  and and_8 (and_8_out, in_1, in_2, in_3);
  or or_1 (out_4[7], and_1_out, and_7_out);
  or or_2 (out_4[5], and_1_out, and_4_out, and_5_out, and_6_out, and_8_out);
  or or_3 (out_4[6], and_2_out, and_7_out, and_4_out);
  or or_4 (out_4[4], and_2_out, and_5_out, and_8_out, and_7_out);
  or or_5 (out_4[3], and_1_out, and_8_out, and_4_out);
  or or_6 (out_4[2], and_2_out, and_4_out, and_6_out, and_7_out, and_8_out);
  or or_7 (out_4[1], and_1_out, and_8_out, and_5_out);
  or or_8 (out_4[0], and_2_out, and_5_out, and_8_out, and_6_out);

  // Notes on the sheet:
  //   Endereço
  //   Palavra
  //   000 -> 10101010
  //   001 -> 01010101
  //   010 ->00000000
  //   011 ->01101100
  //   100 -> 00110011
  //   101 -> 00100101
  //   110 -> 11010100
  //   111 -> 00111111 
endmodule
