// Logisim project Somador8Bits.circ as structural Verilog: 2 circuits, main circuit main
module main (
  input  [7:0] A,
  input  [7:0] B,
  input  CIN,
  output [7:0] out_4,
  output CARRYOUT
);

  wire soma_1_out_5, soma_2_out_5, soma_3_out_5, soma_4_out_5, soma_5_out_5, soma_6_out_5, soma_7_out_5;

  soma soma_1 (.in_1(CIN), .in_2(A[0]), .in_3(B[0]), .out_4(out_4[0]), .out_5(soma_1_out_5));
  soma soma_2 (.in_1(soma_1_out_5), .in_2(A[1]), .in_3(B[1]), .out_4(out_4[1]), .out_5(soma_2_out_5));
  soma soma_3 (.in_1(soma_2_out_5), .in_2(A[2]), .in_3(B[2]), .out_4(out_4[2]), .out_5(soma_3_out_5));
  soma soma_4 (.in_1(soma_3_out_5), .in_2(A[3]), .in_3(B[3]), .out_4(out_4[3]), .out_5(soma_4_out_5));
  soma soma_5 (.in_1(soma_4_out_5), .in_2(A[4]), .in_3(B[4]), .out_4(out_4[4]), .out_5(soma_5_out_5));
  soma soma_6 (.in_1(soma_5_out_5), .in_2(A[5]), .in_3(B[5]), .out_4(out_4[5]), .out_5(soma_6_out_5));
  soma soma_7 (.in_1(soma_6_out_5), .in_2(A[6]), .in_3(B[6]), .out_4(out_4[6]), .out_5(soma_7_out_5));
  soma soma_8 (.in_1(soma_7_out_5), .in_2(A[7]), .in_3(B[7]), .out_4(out_4[7]), .out_5(CARRYOUT));

  // Notes on the sheet:
  //   S
endmodule

module soma (
  input  in_1,
  input  in_2,
  input  in_3,
  output out_4,
  output out_5
);

  wire and_1_out, and_2_out, and_3_out, xor_1_out;

  and and_1 (and_1_out, in_2, in_3);
  and and_2 (and_2_out, in_1, in_2);
  and and_3 (and_3_out, in_3, in_1);
  xor xor_1 (xor_1_out, in_2, in_3);
  or or_1 (out_5, and_1_out, and_2_out, and_3_out);
  xor xor_2 (out_4, xor_1_out, in_1);
endmodule
