// Logisim project Somador8bitsCom4.circ as structural Verilog: 2 circuits, main circuit main
module main (
  input  [7:0] A,
  input  CIN,
  output [7:0] out_3,
  output CARRYOUT
);

  wire soma_1_out_5, soma_2_out_5, soma_3_out_5, soma_4_out_5, soma_5_out_5, soma_6_out_5, soma_7_out_5;

  soma soma_1 (.in_2(A[0]), .in_3(1'b0), .out_4(out_3[0]), .out_5(soma_1_out_5), .in_1(CIN));
  soma soma_2 (.in_2(A[1]), .in_3(1'b0), .out_4(out_3[1]), .out_5(soma_2_out_5), .in_1(soma_1_out_5));
  soma soma_3 (.in_2(A[2]), .in_3(1'b1), .out_4(out_3[2]), .out_5(soma_3_out_5), .in_1(soma_2_out_5));
  soma soma_4 (.in_2(A[3]), .in_3(1'b0), .out_4(out_3[3]), .out_5(soma_4_out_5), .in_1(soma_3_out_5));
  soma soma_5 (.in_2(A[4]), .in_3(1'b0), .out_4(out_3[4]), .out_5(soma_5_out_5), .in_1(soma_4_out_5));
  soma soma_6 (.in_2(A[5]), .in_3(1'b0), .out_4(out_3[5]), .out_5(soma_6_out_5), .in_1(soma_5_out_5));
  soma soma_7 (.in_2(A[6]), .in_3(1'b0), .out_4(out_3[6]), .out_5(soma_7_out_5), .in_1(soma_6_out_5));
  soma soma_8 (.in_2(A[7]), .in_3(1'b0), .out_4(out_3[7]), .out_5(CARRYOUT), .in_1(soma_7_out_5));

  // Notes on the sheet:
  //   S
endmodule

module soma (
  input  in_1,
  input  in_2,
  input  in_3,
  output out_4,
  output out_5
);

  wire and_1_out, and_2_out, and_3_out, xor_1_out;

  xor xor_1 (xor_1_out, in_2, in_3);
  and and_1 (and_1_out, in_2, in_3);
  and and_2 (and_2_out, in_1, in_2);
  and and_3 (and_3_out, in_3, in_1);
  or or_1 (out_5, and_1_out, and_2_out, and_3_out);
  xor xor_2 (out_4, xor_1_out, in_1);
endmodule
